# Fritzing sketch 10b-Keypad_LCD (saved by Fritzing 0.9.2b)

parts:
  LCD1 = LCD screen  # not connected
  Explore_AVR_Breakout_Board1 = Explore AVR Breakout Board  # not connected
  U1 = Explore Ultra One Board [package=THT]

nets:
  N1: U1.pin_154, U1.pin_189
  N2: U1.pin_155, U1.pin_190
  N3: U1.pin_156, U1.pin_191
  N4: U1.pin_158, U1.pin_198
  N5: U1.pin_159, U1.pin_199
  N6: U1.pin_160, U1.pin_200
  N7: U1.pin_161, U1.pin_201
  N8: U1.pin_164, U1.pin_179
  N9: U1.pin_165, U1.pin_178
  N10: U1.pin_166, U1.pin_177
  N11: U1.pin_167, U1.pin_176
  N12: U1.pin_168, U1.pin_175
  N13: U1.pin_169, U1.pin_174
  N14: U1.pin_170, U1.pin_173
  N15: U1.pin_171, U1.pin_172

notes:
  Key Pressed:5
