# Fritzing sketch Interfacing KS0108 based JHD12864E Graphics LCD with Atmega32  (saved by Fritzing 0.9.2b)

parts:
  Explore_AVR_Breakout_Board1 = Explore AVR Breakout Board  # not connected
  U1 = Explore Ultra One Board [package=THT]
  GLCD_128x1 = 128 x 64 Graphic LCD  # not connected

nets:
  N1: U1.pin_102, U1.pin_194
  N2: U1.pin_103, U1.pin_195
  N3: U1.pin_104, U1.pin_196
  N4: U1.pin_105, U1.pin_197
  N5: U1.pin_106, U1.pin_198
  N6: U1.pin_107, U1.pin_199
  N7: U1.pin_108, U1.pin_200
  N8: U1.pin_109, U1.pin_201
  N9: U1.pin_154, U1.pin_189
  N10: U1.pin_155, U1.pin_190
  N11: U1.pin_156, U1.pin_191
  N12: U1.pin_157, U1.pin_192
  N13: U1.pin_158, U1.pin_193
