# Fritzing sketch Interfacing Seven Segment Displays with AVR (saved by Fritzing 0.9.2b)

parts:
  Explore_AVR_Breakout_Board1 = Explore AVR Breakout Board  # not connected
  U1 = Explore Ultra One Board [package=THT]

nets:
  N1: U1.pin_43, U1.pin_154
  N2: U1.pin_44, U1.pin_155
  N3: U1.pin_45, U1.pin_156
  N4: U1.pin_46, U1.pin_157
  N5: U1.pin_47, U1.pin_158
  N6: U1.pin_48, U1.pin_159
  N7: U1.pin_50, U1.pin_160
  N8: U1.pin_51, U1.pin_161
  N9: U1.pin_52, U1.pin_164
  N10: U1.pin_53, U1.pin_165
  N11: U1.pin_54, U1.pin_166
  N12: U1.pin_55, U1.pin_167
