# Fritzing sketch LCD 16X2_AVR (saved by Fritzing 0.9.2b)

parts:
  Explore_AVR_Breakout_Board1 = Explore AVR Breakout Board  # not connected
  LCD1 = LCD screen  # not connected
  U1 = Explore Ultra One Board [package=THT]

nets:
  N1: U1.pin_154, U1.pin_189
  N2: U1.pin_155, U1.pin_190
  N3: U1.pin_156, U1.pin_191
  N4: U1.pin_158, U1.pin_198
  N5: U1.pin_159, U1.pin_199
  N6: U1.pin_160, U1.pin_200
  N7: U1.pin_161, U1.pin_201
