# Fritzing sketch Reading Temperature with AVR ADC (saved by Fritzing 0.9.2b)

parts:
  Explore_AVR_Breakout_Board1 = Explore AVR Breakout Board  # not connected
  U1 = Explore Ultra One Board [package=THT]

nets:
  N1: U1.pin_109, U1.pin_208
  N2: U1.pin_205, U1.pin_206
